// Logisim project Mim_Lab1.circ as structural Verilog: 1 circuit, main circuit main
module main (
  input  A1,
  input  A0,
  input  B1,
  input  B0,
  input  in_5,
  input  [1:0] in_6
);

  wire and_1_out, and_2_out, multiplexer_1_out, multiplexer_2_out, not_1_out, not_2_out, or_1_out, or_2_out,
       xor_1_out, xor_2_out;

  not not_1 (not_1_out, A0);
  xor xor_1 (xor_1_out, B0, A0);
  or or_1 (or_1_out, B0, A0);
  and and_1 (and_1_out, B0, A0);
  Multiplexer #(.enable("true"), .select(2)) multiplexer_1 (
    .in0(and_1_out), .in1(or_1_out), .in2(xor_1_out), .in3(not_1_out), .out(multiplexer_1_out), .sel(in_6),
    .en(in_5));
  LED led_1 (.in(multiplexer_1_out));
  LED led_2 (.in(multiplexer_2_out));
  Multiplexer #(.enable("true"), .select(2)) multiplexer_2 (
    .in0(and_2_out), .in1(or_2_out), .in2(xor_2_out), .in3(not_2_out), .out(multiplexer_2_out), .sel(in_6),
    .en(in_5));
  not not_2 (not_2_out, A1);
  xor xor_2 (xor_2_out, B1, A1);
  or or_2 (or_2_out, B1, A1);
  and and_2 (and_2_out, B1, A1);

  // Notes on the sheet:
  //   select Lines
  //   Enabler
  //   F1
  //   F2
  //   2211404642
  //   Group:06
  //   Jannatul Ferdous Mim
  //   Experiment: 01
endmodule
