// Logisim project Tanjim_Lab1.circ as structural Verilog: 1 circuit, main circuit main
module main (
  input  A1,
  input  B1,
  input  A0,
  input  B0,
  input  [1:0] in_5,
  input  in_6
);

  wire and_1_out, and_2_out, multiplexer_1_out, multiplexer_2_out, not_1_out, not_2_out, or_1_out, or_2_out,
       xor_1_out, xor_2_out;

  not not_1 (not_1_out, A1);
  and and_1 (and_1_out, A0, B0);
  or or_1 (or_1_out, A0, B0);
  xor xor_1 (xor_1_out, A0, B0);
  not not_2 (not_2_out, A0);
  and and_2 (and_2_out, A1, B1);
  or or_2 (or_2_out, A1, B1);
  xor xor_2 (xor_2_out, A1, B1);
  Multiplexer #(.enable("true"), .select(2)) multiplexer_1 (
    .in0(and_2_out), .in1(or_2_out), .in2(xor_2_out), .in3(not_1_out), .out(multiplexer_1_out), .sel(in_5),
    .en(in_6));
  Multiplexer #(.enable("true"), .select(2)) multiplexer_2 (
    .in0(and_1_out), .in1(or_1_out), .in2(xor_1_out), .in3(not_2_out), .out(multiplexer_2_out), .sel(in_5),
    .en(in_6));
  LED led_1 (.in(multiplexer_1_out));
  LED led_2 (.in(multiplexer_2_out));

  // Notes on the sheet:
  //   select Lines
  //   Enabler line
  //   F1
  //   F2
  //   Group: 06
  //   QM Asif Tanjim
  //   2211402042
  //   Experiment: 01
endmodule
