// Logisim project lab2.circ as structural Verilog: 1 circuit, main circuit main
module main (
  input  cin,
  input  A0,
  input  B0,
  input  _0,
  input  _1,
  input  [1:0] S1_S0,
  input  A1,
  input  B1,
  input  _0_2,
  input  _1_2
);

  wire adder_1_cout, adder_1_out, adder_2_cout, adder_2_out, multiplexer_1_out, multiplexer_2_out, not_1_out,
       not_2_out;

  not not_1 (not_1_out, B0);
  not not_2 (not_2_out, B1);
  Multiplexer #(.enable("true"), .select(2)) multiplexer_1 (
    .in0(B0), .in1(not_1_out), .in2(_0), .in3(_1), .out(multiplexer_1_out), .sel(S1_S0));  // open: en
  Multiplexer #(.enable("true"), .select(2)) multiplexer_2 (
    .in0(B1), .in1(not_2_out), .in2(_0_2), .in3(_1_2), .out(multiplexer_2_out), .sel(S1_S0));  // open: en
  Adder #(.width(1)) adder_1 (.a(A0), .b(multiplexer_1_out), .out(adder_1_out), .cin(cin), .cout(adder_1_cout));
  Adder #(.width(1)) adder_2 (
    .a(A1), .b(multiplexer_2_out), .out(adder_2_out), .cin(adder_1_cout), .cout(adder_2_cout));
  LED led_1 (.in(adder_1_out));
  LED led_2 (.in(adder_2_out));
  LED led_3 (.in(adder_2_cout));

  // Notes on the sheet:
  //   D0
  //   D1
  //   Cout
  //   Name:QM Asif Tanjim
  //   ID:2211402042
  //   EXP:02
  //   Group: 04
endmodule
