// Logisim project lab3.circ as structural Verilog: 1 circuit, main circuit main
module main (
  input  shift_right,
  input  I4,
  input  I3,
  input  I2,
  input  shift_left,
  input  I1,
  input  [1:0] Selection,
  output out_8,
  output out_9,
  output out_10,
  output out_11
);

  wire clock_1_out, multiplexer_1_out, multiplexer_2_out, multiplexer_3_out, multiplexer_4_out;

  Multiplexer #(.enable("true"), .select(2)) multiplexer_1 (
    .in0(out_8), .in1(shift_right), .in2(out_9), .in3(I4), .out(multiplexer_1_out), .sel(Selection));  // open: en
  Multiplexer #(.enable("true"), .select(2)) multiplexer_2 (
    .in0(out_9), .in1(out_8), .in2(out_10), .in3(I3), .out(multiplexer_2_out), .sel(Selection));  // open: en
  Multiplexer #(.enable("true"), .select(2)) multiplexer_3 (
    .in0(out_10), .in1(out_9), .in2(out_11), .in3(I2), .out(multiplexer_3_out), .sel(Selection));  // open: en
  Multiplexer #(.enable("true"), .select(2)) multiplexer_4 (
    .in0(out_11), .in1(out_10), .in2(shift_left), .in3(I1), .out(multiplexer_4_out), .sel(Selection));  // open: en
  Clock clock_1 (.out(clock_1_out));
  D_Flip_Flop d_ff_1 (
    .D(multiplexer_1_out), .clk(clock_1_out), .Qn(clock_1_out), .preset(out_8), .reset(out_9));  // open: Q
  D_Flip_Flop d_ff_2 (
    .D(multiplexer_2_out), .clk(clock_1_out), .Q(clock_1_out), .Qn(clock_1_out), .preset(out_9));  // open: reset
  D_Flip_Flop d_ff_3 (.D(multiplexer_3_out), .Q(clock_1_out), .Qn(clock_1_out), .preset(out_10));  // open: clk, reset
  D_Flip_Flop d_ff_4 (
    .D(multiplexer_4_out), .clk(clock_1_out), .Q(clock_1_out), .Qn(clock_1_out), .preset(out_11));  // open: reset
  Button Reset (.out(clock_1_out));

  // Notes on the sheet:
  //   Nowren Mahjabin Khan
  //   2211129642
endmodule
