// Logisim project Lab4.circ as structural Verilog: 1 circuit, main circuit main
module main (
  input  UP,
  input  Down
);

  wire and_1_out, and_2_out, and_3_out, and_4_out, and_5_out, and_6_out, and_7_out, button_1_out,
       clock_1_out, d_ff_1_q, d_ff_1_qn, d_ff_2_q, d_ff_2_qn, d_ff_3_q, d_ff_3_qn, d_ff_4_q, not_1_out,
       or_1_out, or_2_out, or_3_out, or_4_out, xor_1_out, xor_2_out, xor_3_out, xor_4_out;

  not not_1 (not_1_out, UP);
  and and_1 (and_1_out, not_1_out, Down);
  and and_2 (and_2_out, and_1_out, d_ff_1_qn);
  and and_3 (and_3_out, and_2_out, d_ff_2_qn);
  and and_4 (and_4_out, and_3_out, d_ff_3_qn);
  and and_5 (and_5_out, UP, d_ff_1_q);
  and and_6 (and_6_out, and_5_out, d_ff_2_q);
  and and_7 (and_7_out, and_6_out, d_ff_3_q);
  or or_1 (or_1_out, and_6_out, and_3_out);
  or or_2 (or_2_out, and_7_out, and_4_out);
  or or_3 (or_3_out, and_5_out, and_2_out);
  or or_4 (or_4_out, UP, and_1_out);
  xor xor_1 (xor_1_out, d_ff_4_q, or_2_out);
  xor xor_2 (xor_2_out, d_ff_2_q, or_3_out);
  xor xor_3 (xor_3_out, d_ff_3_q, or_1_out);
  xor xor_4 (xor_4_out, d_ff_1_q, or_4_out);
  D_Flip_Flop d_ff_1 (
    .D(xor_4_out), .clk(clock_1_out), .Q(d_ff_1_q), .Qn(d_ff_1_qn), .reset(button_1_out));  // open: preset
  Clock clock_1 (.out(clock_1_out));
  D_Flip_Flop d_ff_2 (
    .D(xor_2_out), .clk(clock_1_out), .Q(d_ff_2_q), .Qn(d_ff_2_qn), .reset(button_1_out));  // open: preset
  D_Flip_Flop d_ff_3 (
    .D(xor_3_out), .clk(clock_1_out), .Q(d_ff_3_q), .Qn(d_ff_3_qn), .reset(button_1_out));  // open: preset
  D_Flip_Flop d_ff_4 (.D(xor_1_out), .clk(clock_1_out), .Q(d_ff_4_q), .reset(button_1_out));  // open: Qn, preset
  Button button_1 (.out(button_1_out));
  LED led_1 (.in(d_ff_1_q));
  LED led_2 (.in(d_ff_2_q));
  LED led_3 (.in(d_ff_3_q));
  LED led_4 (.in(d_ff_4_q));

  // Notes on the sheet:
  //   Clock
  //   Reset
  //   A0
  //   A1
  //   A2
  //   A3
  //   EXP:04
  //   ID: 2211402042
  //   Group:06
  //   CSE332L
  //   Name: QM Asif Tanjim
endmodule
