// Logisim project lab5.circ as structural Verilog: 1 circuit, main circuit Register_File_93103648
module Register_File_93103648 (
  input  [15:0] Write_Data_b3affb6d,
  input  [3:0] Read_Register_Number_1_74a6368c,
  input  [3:0] in_3,
  input  [3:0] Read_Register_Number_2_77320616,
  input  Write_Control_c57610ad,
  output [15:0] Read_Data_1_714079f6,
  output [15:0] Read_Data_2_a2121d80
);

  wire and_1_out, and_2_out, and_3_out, and_4_out, and_5_out, and_6_out, and_7_out, and_8_out, and_9_out,
       and_10_out, and_11_out, and_12_out, and_13_out, and_14_out, and_15_out, and_16_out, clock_1_out,
       decoder_1_out0, decoder_1_out1, decoder_1_out2, decoder_1_out3, decoder_1_out4, decoder_1_out5,
       decoder_1_out6, decoder_1_out7, decoder_1_out8, decoder_1_out9, decoder_1_out10, decoder_1_out11,
       decoder_1_out12, decoder_1_out13, decoder_1_out14, decoder_1_out15;
  wire [15:0] register_1_q, register_2_q, register_3_q, register_4_q, register_5_q, register_6_q,
       register_7_q, register_8_q, register_9_q, register_10_q, register_11_q, register_12_q, register_14_q,
       register_15_q, register_16_q, undriven, undriven_2, undriven_3, undriven_4, undriven_5, undriven_6,
       undriven_7, undriven_8, undriven_9, undriven_10, undriven_11;

  Decoder #(.select(4)) decoder_1 (
    .out0(decoder_1_out0), .out1(decoder_1_out1), .out2(decoder_1_out2), .out3(decoder_1_out3),
    .out4(decoder_1_out4), .out5(decoder_1_out5), .out6(decoder_1_out6), .out7(decoder_1_out7),
    .out8(decoder_1_out8), .out9(decoder_1_out9), .out10(decoder_1_out10), .out11(decoder_1_out11),
    .out12(decoder_1_out12), .out13(decoder_1_out13), .out14(decoder_1_out14), .out15(decoder_1_out15),
    .sel(in_3));  // open: en
  and and_1 (and_1_out, Write_Control_c57610ad, decoder_1_out0);
  and and_2 (and_2_out, Write_Control_c57610ad, decoder_1_out1);
  and and_3 (and_3_out, Write_Control_c57610ad, decoder_1_out2);
  and and_4 (and_4_out, Write_Control_c57610ad, decoder_1_out3);
  and and_5 (and_5_out, Write_Control_c57610ad, decoder_1_out4);
  and and_6 (and_6_out, Write_Control_c57610ad, decoder_1_out5);
  and and_7 (and_7_out, Write_Control_c57610ad, decoder_1_out6);
  and and_8 (and_8_out, Write_Control_c57610ad, decoder_1_out7);
  and and_9 (and_9_out, Write_Control_c57610ad, decoder_1_out8);
  and and_10 (and_10_out, Write_Control_c57610ad, decoder_1_out9);
  and and_11 (and_11_out, Write_Control_c57610ad, decoder_1_out10);
  and and_12 (and_12_out, Write_Control_c57610ad, decoder_1_out11);
  and and_13 (and_13_out, Write_Control_c57610ad, decoder_1_out12);
  and and_14 (and_14_out, Write_Control_c57610ad, decoder_1_out13);
  and and_15 (and_15_out, Write_Control_c57610ad, decoder_1_out14);
  and and_16 (and_16_out, Write_Control_c57610ad, decoder_1_out15);
  Clock clock_1 (.out(clock_1_out));
  Register #(.width(16)) register_1 (
    .D(Write_Data_b3affb6d), .en(and_2_out), .clk(clock_1_out), .Q(register_1_q));  // open: clr
  Register #(.width(16)) register_2 (
    .D(Write_Data_b3affb6d), .en(and_4_out), .clk(clock_1_out), .Q(register_2_q));  // open: clr
  Register #(.width(16)) register_3 (
    .D(Write_Data_b3affb6d), .en(and_8_out), .Q(register_3_q), .clk(clock_1_out));  // open: clr
  Register #(.width(16)) register_4 (
    .D(Write_Data_b3affb6d), .en(and_9_out), .Q(register_4_q), .clk(clock_1_out));  // open: clr
  Register #(.width(16)) register_5 (
    .D(Write_Data_b3affb6d), .en(and_10_out), .Q(register_5_q), .clk(clock_1_out));  // open: clr
  Register #(.width(16)) register_6 (
    .D(Write_Data_b3affb6d), .en(and_11_out), .Q(register_6_q), .clk(clock_1_out));  // open: clr
  Register #(.width(16)) register_7 (
    .D(Write_Data_b3affb6d), .en(and_12_out), .Q(register_7_q), .clk(clock_1_out));  // open: clr
  Register #(.width(16)) register_8 (
    .D(Write_Data_b3affb6d), .en(and_13_out), .Q(register_8_q), .clk(clock_1_out));  // open: clr
  Register #(.width(16)) register_9 (
    .D(Write_Data_b3affb6d), .en(and_14_out), .Q(register_9_q), .clk(clock_1_out));  // open: clr
  Register #(.width(16)) register_10 (
    .D(Write_Data_b3affb6d), .en(and_15_out), .Q(register_10_q), .clk(clock_1_out));  // open: clr
  Register #(.width(16)) register_11 (
    .D(Write_Data_b3affb6d), .en(and_16_out), .Q(register_11_q), .clk(clock_1_out));  // open: clr
  Register #(.width(16)) register_12 (
    .D(Write_Data_b3affb6d), .en(and_6_out), .clk(clock_1_out), .Q(register_12_q));  // open: clr
  // Register #(.width(16)) register_13: pin names not known; wires that end beside it: register_4_q, register_5_q
  Register #(.width(16)) register_14 (
    .D(Write_Data_b3affb6d), .en(and_3_out), .clk(clock_1_out), .Q(register_14_q));  // open: clr
  Register #(.width(16)) register_15 (
    .D(Write_Data_b3affb6d), .en(and_5_out), .clk(clock_1_out), .Q(register_15_q));  // open: clr
  Register #(.width(16)) register_16 (
    .D(Write_Data_b3affb6d), .en(and_1_out), .clk(clock_1_out), .Q(register_16_q));  // open: clr
  Multiplexer #(.enable("true"), .select(4), .width(16)) multiplexer_1 (
    .in0(register_16_q), .in1(register_1_q), .in2(register_14_q), .in3(register_2_q), .in4(register_15_q),
    .in5(register_12_q), .out(Read_Data_1_714079f6), .sel(Read_Register_Number_1_74a6368c));  // open: in6, in7, in8, in9, in10, in11, in12, in13, in14, in15, en
  Multiplexer #(.enable("true"), .select(4), .width(16)) multiplexer_2 (
    .in0(register_16_q), .in1(register_1_q), .in2(register_14_q), .in3(register_2_q), .in4(register_15_q),
    .in5(undriven_11), .in6(undriven_10), .in7(undriven_9), .in8(undriven_8), .in9(undriven_7),
    .in10(undriven_6), .in11(undriven_5), .in12(undriven_4), .in13(undriven_3), .in14(undriven_2),
    .in15(undriven), .out(Read_Data_2_a2121d80), .sel(Read_Register_Number_2_77320616));  // open: en
endmodule
